// Logisim project cpu.circ as structural Verilog: 2 circuits, main circuit cpu
module cpu (
  input  clk,
  input  [31:0] INSTRUCTION,
  input  [31:0] READ_DATA,
  output [31:0] WRITE_ADDRESS,
  output [31:0] PROGRAM_COUNTER,
  output [31:0] ra,
  output [31:0] sp,
  output [31:0] t0,
  output [31:0] t1,
  output [31:0] t2,
  output [31:0] s0,
  output [31:0] s1,
  output [31:0] a0,
  output [31:0] tohost,
  output [3:0] WRITE_ENABLE,
  output [31:0] WRITE_DATA
);

  wire and_1_out, ASel, BrEq, BrLt, BrUn, BSel, CSRSel, CSRWen, MemRW, PCSel, RegWEn;
  wire [1:0] WBSel;
  wire [2:0] ImmSel;
  wire [3:0] ALUSel;
  wire [31:0] adder_1_out, adder_2_out, alu_WB, imm, imm_EX, imm_MEM, imm_WB, inst_EX, inst_ID, inst_MEM,
       mem_WB, multiplexer_1_out, multiplexer_2_out, multiplexer_3_out, PC, PC_EX, PC_ID, PC_MEM, PCadd4_WB,
       READ_DATA_Selected, ReadData1, ReadData2, Result, rs1_EX, rs2_EX, WriteData;

  Adder #(.width(32)) adder_1 (.a(PROGRAM_COUNTER), .b(32'h4), .out(adder_1_out));  // open: cin, cout
  Multiplexer #(.enable("false"), .width(32)) multiplexer_1 (
    .in0(adder_1_out), .in1(Result), .out(multiplexer_1_out), .sel(PCSel));
  Register #(.width(32)) u_PC (.D(multiplexer_1_out), .en(1'b1), .clk(clk), .Q(PROGRAM_COUNTER));  // open: clr
  Register #(.width(32)) u_PC_ID (.D(PROGRAM_COUNTER), .en(1'b1), .clk(clk), .Q(PC_ID));  // open: clr
  Register #(.width(32)) u_inst_ID (.D(INSTRUCTION), .en(1'b1), .clk(clk), .Q(inst_ID));  // open: clr
  control_logic control_logic_1 (
    .inst(inst_ID), .BrEq(BrEq), .BrLt(BrLt), .PCSel(PCSel), .RegWEn(RegWEn), .ImmSel(ImmSel), .BrUn(BrUn),
    .ASel(ASel), .BSel(BSel), .ALUSel(ALUSel), .MemRW(MemRW), .WBSel(WBSel), .CSRSel(CSRSel), .CSRWen(CSRWen));
  imm_gen imm_gen_1 (.inst(inst_ID), .ImmSel(ImmSel), .imm(imm));
  and and_1 (and_1_out, CSRSel, CSRWen);
  regfile regfile_1 (
    .rs1(inst_ID[19:15]), .rs2(inst_ID[24:20]), .rd(inst_ID[11:7]), .Write_Data(WriteData), .RegWEn(RegWEn),
    .clk(clk), .ra(ra), .sp(sp), .t0(t0), .t1(t1), .t2(t2), .s0(s0), .s1(s1), .a0(a0),
    .Read_Data_1(ReadData1), .Read_Data_2(ReadData2));
  csr csr_1 (.CSR_address(12'h51e), .CSR_din(ReadData1), .CSR_WE(and_1_out), .clk(clk), .tohost(tohost));
  Register #(.width(32)) u_PC_EX (.D(PC_ID), .en(1'b1), .clk(clk), .Q(PC_EX));  // open: clr
  Register #(.width(32)) u_RS1_EX (.D(ReadData1), .en(1'b1), .clk(clk), .Q(rs1_EX));  // open: clr
  Register #(.width(32)) u_RS2_EX (.D(ReadData2), .en(1'b1), .clk(clk), .Q(rs2_EX));  // open: clr
  Register #(.width(32)) u_imm_EX (.D(imm), .en(1'b1), .clk(clk), .Q(imm_EX));  // open: clr
  Register #(.width(32)) u_inst_EX (.D(inst_ID), .en(1'b1), .clk(clk), .Q(inst_EX));  // open: clr
  branch_comp branch_comp_1 (.rs1(rs1_EX), .rs2(rs2_EX), .BrUn(BrUn), .BrEq(BrEq), .BrLt(BrLt));
  Multiplexer #(.enable("false"), .width(32)) multiplexer_2 (
    .in0(rs1_EX), .in1(PC), .out(multiplexer_2_out), .sel(ASel));
  Multiplexer #(.enable("false"), .width(32)) multiplexer_3 (
    .in0(rs2_EX), .in1(imm_EX), .out(multiplexer_3_out), .sel(BSel));
  alu alu_1 (.Result(Result), .A(multiplexer_2_out), .B(multiplexer_3_out), .ALUSel(ALUSel));
  Register #(.width(32)) u_PC_MEM (.D(PC_EX), .en(1'b1), .clk(clk), .Q(PC_MEM));  // open: clr
  Register #(.width(32)) alu_MEM (.D(Result), .en(1'b1), .clk(clk), .Q(WRITE_ADDRESS));  // open: clr
  Register #(.width(32)) rs2_MEM (.D(rs2_EX), .en(1'b1), .clk(clk), .Q(WRITE_DATA));  // open: clr
  Register #(.width(32)) u_inst_MEM (.D(inst_EX), .en(1'b1), .clk(clk), .Q(inst_MEM));  // open: clr
  DMEM dmem_1 (
    .Mem_RW(MemRW), .inst(inst_MEM), .alu_result(WRITE_ADDRESS), .READ_DATA(READ_DATA),
    .WRITE_EN(WRITE_ENABLE), .READ_DATA_Selected(READ_DATA_Selected));
  Adder #(.width(32)) adder_2 (.a(PC_MEM), .b(32'h4), .out(adder_2_out));  // open: cin, cout
  Register #(.width(32)) u_PCadd4_WB (.D(adder_2_out), .en(1'b1), .clk(clk), .Q(PCadd4_WB));  // open: clr
  Register #(.width(32)) u_alu_WB (.D(WRITE_ADDRESS), .en(1'b1), .clk(clk), .Q(alu_WB));  // open: clr
  Register #(.width(32)) u_mem_WB (.D(READ_DATA_Selected), .en(1'b1), .clk(clk), .Q(mem_WB));  // open: clr
  Register #(.width(32)) inst_WB (.D(imm_MEM), .en(1'b1), .clk(clk), .Q(imm_WB));  // open: clr
  Multiplexer #(.enable("false"), .select(2), .width(32)) multiplexer_4 (
    .in0(mem_WB), .in1(alu_WB), .in2(PCadd4_WB), .out(WriteData), .sel(WBSel));  // open: in3

  // Other names for the same wires on the sheet: alu_MEM[31:0] = WRITE_ADDRESS; rd[4:0] = inst_ID[11:7];
  //   rs1[4:0] = inst_ID[19:15]; rs2[4:0] = inst_ID[24:20]; rs2_MEM[31:0] = WRITE_DATA

  // Notes on the sheet:
  //   Output to IMEM
  //   IMEM (do **NOT** move this)
  //   Inputs from IMEM
  //   It is OK to move the PC, RegFile, ALU, MEM, Branch Comp, Imm Gen, and Control Logic to wherever is most convenient for you when constructing your CPU, and to delete this text
  //   Inputs/Outputs for testing. Do **NOT** move these.
  //   Outputs To DMEM
  //   DMEM (do **NOT** move this)
  //   Inputs From DMEM
endmodule

module DMEM (
  input  Mem_RW,
  input  [31:0] inst,
  input  [31:0] alu_result,
  input  [31:0] READ_DATA,
  output [3:0] WRITE_EN,
  output [31:0] READ_DATA_Selected
);

  wire comparator_1_eq, comparator_2_eq, comparator_3_eq, comparator_4_eq, is_lb_out, is_lh_out, is_sb_out,
       is_sh_out, is_sw_out, isSType, not_1_out, not_2_out, not_3_out, not_4_out, not_5_out, not_6_out,
       not_7_out, not_8_out, not_9_out, not_10_out, not_11_out, not_12_out, not_13_out, not_14_out,
       not_15_out, not_16_out, not_17_out, not_18_out, not_19_out, not_20_out, Sel_0001, Sel_0010, Sel_0011,
       Sel_0100, Sel_1000, Sel_1100, Sel_1111;
  wire [31:0] multiplexer_1_out, READ_DATA_8bits, READ_DATA_16bits;

  not not_1 (not_1_out, inst[6]);
  not not_2 (not_2_out, inst[14]);
  not not_3 (not_3_out, inst[13]);
  not not_4 (not_4_out, inst[12]);
  and is_sb (is_sb_out, isSType, not_2_out, not_3_out, not_4_out);
  not not_5 (not_5_out, inst[4]);
  not not_6 (not_6_out, inst[3]);
  not not_7 (not_7_out, inst[2]);
  and and_1 (isSType, not_1_out, inst[5], not_5_out, not_6_out, not_7_out, inst[1], inst[0]);
  not not_8 (not_8_out, inst[14]);
  not not_9 (not_9_out, inst[13]);
  and is_sh (is_sh_out, isSType, not_8_out, not_9_out, inst[12]);
  not not_10 (not_10_out, inst[14]);
  not not_11 (not_11_out, inst[12]);
  and is_sw (is_sw_out, isSType, not_10_out, inst[13], not_11_out);
  not not_12 (not_12_out, alu_result[1]);
  not not_13 (not_13_out, alu_result[0]);
  not not_14 (not_14_out, alu_result[1]);
  not not_15 (not_15_out, alu_result[0]);
  not not_16 (not_16_out, alu_result[0]);
  not not_17 (not_17_out, alu_result[1]);
  not not_18 (not_18_out, alu_result[0]);
  not not_19 (not_19_out, alu_result[1]);
  not not_20 (not_20_out, alu_result[0]);
  and sw (Sel_1111, is_sw_out, not_12_out, not_13_out);
  and sh_h (Sel_0011, is_sh_out, not_14_out, not_15_out);
  and sh_l (Sel_1100, is_sh_out, alu_result[1], not_16_out);
  and sb_0 (Sel_0001, is_sb_out, not_17_out, not_18_out);
  and sb_1 (Sel_0010, is_sb_out, not_19_out, alu_result[0]);
  and sb_2 (Sel_0100, is_sb_out, alu_result[1], not_20_out);
  and sb_3 (Sel_1000, is_sb_out, alu_result[1], alu_result[0]);
  assign WRITE_EN = Mem_RW ? 4'b0000 : 4'bz;  // Controlled_Buffer controlled_buffer_1
  assign WRITE_EN = Sel_0001 ? 4'b0001 : 4'bz;  // Controlled_Buffer controlled_buffer_2
  assign WRITE_EN = Sel_0010 ? 4'b0010 : 4'bz;  // Controlled_Buffer controlled_buffer_3
  assign WRITE_EN = Sel_0011 ? 4'b0011 : 4'bz;  // Controlled_Buffer controlled_buffer_4
  assign WRITE_EN = Sel_0100 ? 4'b0100 : 4'bz;  // Controlled_Buffer controlled_buffer_5
  assign WRITE_EN = Sel_1000 ? 4'b1000 : 4'bz;  // Controlled_Buffer controlled_buffer_6
  assign WRITE_EN = Sel_1100 ? 4'b1100 : 4'bz;  // Controlled_Buffer controlled_buffer_7
  assign WRITE_EN = Sel_1111 ? 4'b1111 : 4'bz;  // Controlled_Buffer controlled_buffer_8
  Comparator #(.width(7)) comparator_1 (.a(inst[6:0]), .eq(comparator_1_eq));  // open: b, gt, lt
  Comparator #(.width(3)) comparator_2 (.a(inst[14:12]), .b(3'b001), .eq(comparator_2_eq));  // open: gt, lt
  Multiplexer #(.enable("false"), .width(32)) multiplexer_1 (
    .in0(READ_DATA), .in1(READ_DATA_16bits), .out(multiplexer_1_out), .sel(is_lh_out));
  and is_lh (is_lh_out, comparator_1_eq, comparator_2_eq);
  assign READ_DATA_8bits = {{24{READ_DATA[7]}}, READ_DATA[7:0]};  // Bit_Extender bit_extender_1
  assign READ_DATA_16bits = {{16{READ_DATA[15]}}, READ_DATA[15:0]};  // Bit_Extender bit_extender_2
  Comparator #(.width(7)) comparator_3 (.a(inst[6:0]), .b(7'b0000011), .eq(comparator_3_eq));  // open: gt, lt
  Comparator #(.width(3)) comparator_4 (.a(inst[14:12]), .b(3'b000), .eq(comparator_4_eq));  // open: gt, lt
  and is_lb (is_lb_out, comparator_3_eq, comparator_4_eq);
  Multiplexer #(.enable("false"), .width(32)) multiplexer_2 (
    .in0(multiplexer_1_out), .in1(READ_DATA_8bits), .out(READ_DATA_Selected), .sel(is_lb_out));

  // Other names for the same wires on the sheet: READ_DATA_32bits[31:0] = READ_DATA; alu_0 = alu_result[0];
  //   alu_1 = alu_result[1]; inst_MEM[31:0] = inst; opcode[6:0] = inst[6:0]; opcode0 = inst[0]; opcode1 = inst[1];
  //   opcode2 = inst[2]; opcode3 = inst[3]; opcode4 = inst[4]; opcode5 = inst[5]; opcode6 = inst[6];
  //   funct3[2:0] = inst[14:12]; funct3_0 = inst[12]; funct3_1 = inst[13]; funct3_2 = inst[14];
  //   funct7[6:0] = inst[31:25]
endmodule
